# Fritzing sketch schema (saved by Fritzing 0.8.5b)
breadboards: 1

parts:
  U1 = attiny85 [package=dip]
  LED1 = LED - 3mm [color="Red (633nm)" package="3 mm [THT]"]
  R1 = Resistor [tolerance=±5% resistance=1k package=THT]
  DS1 = DS18B20 1-Wire Temperature Sensor [part_number=DS18B20]
  R2 = Resistor [tolerance=±5% resistance=4.7k package=THT]
  U2 = mystery part, 3 pins [chip_label=FS100A]
  S4 = SWITCH-MOMENTARY-2 [package=tactile-pth-12mm]

nets:
  N1: U1.Pin_1, S4.2
  N2: U1.Pin_2, LED1.anode
  GND: U1.Pin_4, R1.Pin_1, DS1.GND, U2.pin3, S4.1
  N3: U1.Pin_5, DS1.DQ, R2.Pin_1
  N4: U1.Pin_6, U2.pin1
  5V: U1.Pin_8, DS1.VDD, R2.Pin_0, U2.pin2
  N5: LED1.cathode, R1.Pin_0
